# Fritzing sketch Sketch (saved by Fritzing 0.9.9b)
breadboards: 1

parts:
  U1 = ESP8266 WiFi Module [part_number=ESP8266]  # not connected
  Gizwits_WiFi_Witty_ESP-12F1 = Gizwits WiFi Witty ESP-12F  # not connected
  Gizwits_WiFi_Witty_ESP-12F2 = Gizwits WiFi Witty ESP-12F  # not connected
  U2 = ESP8266 NodeMCU LoLin module
  Компонент2 = BME280
  sdCard1 = my_sdCard

nets:
  N1: U2.D1, Компонент2.SCL
  N2: U2.D2, Компонент2.SDA
  3V3: U2.3V3, Компонент2.VIN, sdCard1.3V3
  GND: U2.GND, Компонент2.GND, sdCard1.GND
  N3: U2.D5, sdCard1.CLK
  N4: U2.D6, sdCard1.MISO
  N5: U2.D7, sdCard1.MOSI
  N6: U2.D8, sdCard1.CS

custom parts:
  ESP8266 NodeMCU LoLin module: ESP8266 based NodeMCU
  my_sdCard: micro sdCard Adapter with 90º pin header. Use a filtering Capacitor between CS and GND if needed. PCB View Pinouts are Reversed for laying parallel on PCB using a 90º pin header.
